# Fritzing sketch Placa (saved by Fritzing 0.9.3b)
circuit board: 8.46667cm x 5.64444cm
breadboards: 1

parts:
  Gizwits_WiFi_Witty_ESP-12F1 = Gizwits WiFi Witty ESP-12F
  Trimpot_LDR = TRIMPOT [package=3362u-2]
  D1 = Diode [package=diode-1n4001]
  Temp = DS18B20 1-Wire Temperature Sensor [part_number=DS18B20]
  LED_AGUA = LED - 5mm [color="Red (633nm)" package="5 mm [THT]"]
  LED_STATUS = LED - 5mm [color="Green (570nm)" package="5 mm [THT]"]
  Humedad_del_suelo = Soil Moisture Sensor
  Trimpot_Temp = TRIMPOT [package=3362u-2]
  D3 = Diode [package=diode-1n4001]
  R6 = Resistor [tolerance=±5% resistance=220 package=THT]
  R4 = Resistor [tolerance=±5% resistance=220 package=THT]
  R3 = Resistor [tolerance=±5% resistance=220 package=THT]
  R2 = Photocell (LDR) [package=THT]

nets:
  N1: Gizwits_WiFi_Witty_ESP-12F1.ADC, D1.C, D3.C
  N2: Gizwits_WiFi_Witty_ESP-12F1.GPIO12, Gizwits_WiFi_Witty_ESP-12F1.GPIO13, Humedad_del_suelo.VCC
  VCC: Gizwits_WiFi_Witty_ESP-12F1.VCC, Gizwits_WiFi_Witty_ESP-12F1.GPIO2, Temp.VDD, R4.Pin_0
  GND: Gizwits_WiFi_Witty_ESP-12F1.GND, Trimpot_LDR.CW, D1.A, Temp.GND, LED_AGUA.anode, LED_STATUS.anode, Humedad_del_suelo.GND, Trimpot_Temp.WIPER, Trimpot_Temp.CW, R6.Pin_0, R6.Pin_1, R3.Pin_0
  N3: Gizwits_WiFi_Witty_ESP-12F1.GPIO15, Trimpot_LDR.CCW
  N4: Gizwits_WiFi_Witty_ESP-12F1.GPIO0, LED_AGUA.cathode
  N5: Gizwits_WiFi_Witty_ESP-12F1.GPIO5, LED_STATUS.cathode
  N6: Gizwits_WiFi_Witty_ESP-12F1.RXD, Gizwits_WiFi_Witty_ESP-12F1.TXD
  N7: Trimpot_LDR.WIPER, R2.pin_0
  N8: Temp.DQ, R4.Pin_1
  N9: Humedad_del_suelo.SIG, Trimpot_Temp.CCW
  N10: D3.A, R3.Pin_1, R2.pin_1
